// Logisim project Lab05_Counter.circ as structural Verilog: 7 circuits, main circuit main
module main (
  input  rst,
  input  [2:0] sel
);

  wire clk_out;
  wire [3:0] universal_1_res;

  Clock #(.highDuration(4), .lowDuration(4)) clk (.out(clk_out));
  Clock sysclk ();  // open: out
  // Probe on universal_1_res
  Universal universal_1 (.clk(clk_out), .rst(rst), .sel(sel), .res(universal_1_res));
  Hex_Digit_Display hex_digit_display_1 (.value(universal_1_res));  // open: dp
endmodule

module UpCounter (
  input  clk,
  input  rst,
  output [3:0] Up
);

  wire d_ff_1_qn, d_ff_2_qn, d_ff_3_qn, d_ff_4_qn;

  D_Flip_Flop d_ff_1 (.D(d_ff_1_qn), .clk(clk), .Q(Up[0]), .Qn(d_ff_1_qn), .reset(rst));  // open: preset
  D_Flip_Flop d_ff_2 (.D(d_ff_2_qn), .clk(d_ff_1_qn), .Q(Up[1]), .Qn(d_ff_2_qn), .reset(rst));  // open: preset
  D_Flip_Flop d_ff_3 (.D(d_ff_3_qn), .clk(d_ff_2_qn), .Q(Up[2]), .Qn(d_ff_3_qn), .reset(rst));  // open: preset
  D_Flip_Flop d_ff_4 (.D(d_ff_4_qn), .clk(d_ff_3_qn), .Q(Up[3]), .Qn(d_ff_4_qn), .reset(rst));  // open: preset
endmodule

module DownCounter (
  input  clk,
  input  rst,
  output [3:0] Down
);

  wire d_ff_1_qn, d_ff_2_qn, d_ff_3_qn, d_ff_4_qn;

  D_Flip_Flop d_ff_1 (.D(d_ff_1_qn), .clk(clk), .Q(Down[0]), .Qn(d_ff_1_qn), .preset(rst));  // open: reset
  D_Flip_Flop d_ff_2 (.D(d_ff_2_qn), .clk(Down[0]), .Q(Down[1]), .Qn(d_ff_2_qn), .preset(rst));  // open: reset
  D_Flip_Flop d_ff_3 (.D(d_ff_3_qn), .clk(Down[1]), .Q(Down[2]), .Qn(d_ff_3_qn), .preset(rst));  // open: reset
  D_Flip_Flop d_ff_4 (.D(d_ff_4_qn), .clk(Down[2]), .Q(Down[3]), .Qn(d_ff_4_qn), .preset(rst));  // open: reset
endmodule

module DecadeCounter (
  input  clk,
  input  rst,
  output [3:0] Decade
);

  wire and_1_out, d_ff_1_qn, d_ff_2_qn, d_ff_3_qn, d_ff_4_qn, or_1_out;

  D_Flip_Flop d_ff_1 (.D(d_ff_1_qn), .clk(clk), .Q(Decade[0]), .Qn(d_ff_1_qn), .reset(or_1_out));  // open: preset
  or or_1 (or_1_out, rst, and_1_out);
  D_Flip_Flop d_ff_2 (.D(d_ff_2_qn), .clk(d_ff_1_qn), .Q(Decade[1]), .Qn(d_ff_2_qn), .reset(or_1_out));  // open: preset
  D_Flip_Flop d_ff_3 (.D(d_ff_3_qn), .clk(d_ff_2_qn), .Q(Decade[2]), .Qn(d_ff_3_qn), .reset(or_1_out));  // open: preset
  D_Flip_Flop d_ff_4 (.D(d_ff_4_qn), .clk(d_ff_3_qn), .Q(Decade[3]), .Qn(d_ff_4_qn), .reset(or_1_out));  // open: preset
  and and_1 (and_1_out, Decade[1], Decade[3]);
endmodule

module RingCounter (
  input  clk,
  input  rst,
  output [3:0] Ring
);

  D_Flip_Flop d_ff_1 (.D(Ring[3]), .clk(clk), .Q(Ring[0]), .preset(rst));  // open: Qn, reset
  D_Flip_Flop d_ff_2 (.D(Ring[0]), .clk(clk), .Q(Ring[1]), .reset(rst));  // open: Qn, preset
  D_Flip_Flop d_ff_3 (.D(Ring[1]), .clk(clk), .Q(Ring[2]), .reset(rst));  // open: Qn, preset
  D_Flip_Flop d_ff_4 (.D(Ring[2]), .clk(clk), .Q(Ring[3]), .reset(rst));  // open: Qn, preset
endmodule

module JohnsonCounter (
  input  clk,
  input  rst,
  output [3:0] Johnson
);

  wire d_ff_4_qn;

  D_Flip_Flop d_ff_1 (.D(d_ff_4_qn), .clk(clk), .Q(Johnson[0]), .preset(rst));  // open: Qn, reset
  D_Flip_Flop d_ff_2 (.D(Johnson[0]), .clk(clk), .Q(Johnson[1]), .reset(rst));  // open: Qn, preset
  D_Flip_Flop d_ff_3 (.D(Johnson[1]), .clk(clk), .Q(Johnson[2]), .reset(rst));  // open: Qn, preset
  D_Flip_Flop d_ff_4 (.D(Johnson[2]), .clk(clk), .Q(Johnson[3]), .Qn(d_ff_4_qn), .reset(rst));  // open: preset
endmodule

module Universal (
  input  clk,
  input  rst,
  input  [2:0] sel,
  output [3:0] res
);

  wire [3:0] decadecounter_1_decade, downcounter_1_down, johnsoncounter_1_johnson, ringcounter_1_ring,
       upcounter_1_up;

  UpCounter upcounter_1 (.clk(clk), .rst(rst), .Up(upcounter_1_up));
  DownCounter downcounter_1 (.clk(clk), .rst(rst), .Down(downcounter_1_down));
  DecadeCounter decadecounter_1 (.clk(clk), .rst(rst), .Decade(decadecounter_1_decade));
  RingCounter ringcounter_1 (.clk(clk), .rst(rst), .Ring(ringcounter_1_ring));
  JohnsonCounter johnsoncounter_1 (.clk(clk), .rst(rst), .Johnson(johnsoncounter_1_johnson));
  Multiplexer #(.select(3), .width(4)) multiplexer_1 (
    .in0(upcounter_1_up), .in1(downcounter_1_down), .in2(decadecounter_1_decade), .in3(ringcounter_1_ring),
    .in4(johnsoncounter_1_johnson), .out(res), .sel(sel));  // open: in5, in6, in7
endmodule
